# Fritzing sketch snort (saved by Fritzing 0.8.3b)
breadboards: 1

parts:
  Raspberry_Pi_rev1 = Raspberry Pi rev1
  BUTTON1 = Waterproof Pushbutton (red)
  R1 = Resistor [tolerance=±5% resistance=330 package=THT]
  R2 = Resistor [tolerance=±5% resistance=10k package=THT]
  R3 = Resistor [tolerance=±5% resistance=10k package=THT]
  PIR1 = PIR sensor
  R4 = Resistor [tolerance=±5% resistance=10k package=THT]

nets:
  3V3: Raspberry_Pi_rev1.3V3, BUTTON1.no_name_yet#1, PIR1.VDD
  GND: Raspberry_Pi_rev1.GND, BUTTON1.no_name_yet#5, PIR1.GND
  N1: Raspberry_Pi_rev1.GPIO_23, R1.Pin_1
  N2: Raspberry_Pi_rev1.GPIO_21, R2.Pin_1
  N3: Raspberry_Pi_rev1.GPIO22, R3.Pin_1
  N4: Raspberry_Pi_rev1.GPIO_25, R4.Pin_1
  N5: BUTTON1.no_name_yet#2, R3.Pin_0
  N6: BUTTON1.no_name_yet#3, R2.Pin_0
  N7: BUTTON1.no_name_yet#4, R1.Pin_0
  N8: PIR1.SIG, R4.Pin_0

custom parts:
  Waterproof Pushbutton (red): Waterproof Illuminated Pushbutton (red)
